# Fritzing sketch minivactrol (saved by Fritzing 1.0.2b)
circuit board: 1cm x 2cm
breadboards: 1

parts:
  J7 = female pin header, 2 pins [form="♀ (female)"]
  J8 = female pin header, 2 pins [form="♀ (female)"]
  J9 = female pin header, 2 pins [form="♀ (female)"]
  J10 = female pin header, 2 pins [form="♀ (female)"]
  LED3 = LED - 3mm [color="Red (633nm)" current=0.030A package="3 mm [THT]"]
  R6 = Resistor [tolerance=±5% resistance=220 power=0.25W package=THT]
  J11 = female pin header, 2 pins [form="♀ (female)"]

nets:
  N1: J7.pin1, J9.pin1, LED3.cathode
  N2: J7.pin2, J9.pin2, R6.Pin_1
  N3: J8.pin1, J10.pin1, J11.pin1
  N4: J8.pin2, J10.pin2, J11.pin2
  N5: LED3.anode, R6.Pin_0
